# Fritzing sketch rasp-ada (saved by Fritzing 0.9.3b)
breadboards: 1

parts:
  Raspberry_Pi1 = Raspberry Pi 2
  R3 = Resistor [tolerance=±5% resistance=330 package=THT]
  R4 = Resistor [tolerance=±5% resistance=330 package=THT]
  LED3 = LED - 5mm [color="Red (633nm)" package="5 mm [THT]"]
  LED4 = LED - 5mm [color="Green (565nm)" package="5 mm [THT]"]
  Q2 = MOSFET-NCHANNEL [package=to220v]
  D1 = Diode [package=diode-1n4001]
  D2 = Diode [package=diode-1n4001]
  BAT1 = BC9VPC [package=bc9vpc]
  L1 = Solenoid

nets:
  N1: Raspberry_Pi1.GPIO17, LED4.cathode
  N2: Raspberry_Pi1.GPIO27, LED3.cathode
  N3: Raspberry_Pi1.GPIO22, D2.A
  N4: Raspberry_Pi1.GND, R3.Pin_0, R4.Pin_0, Q2.S, BAT1.V-
  N5: R3.Pin_1, LED3.anode
  N6: R4.Pin_1, LED4.anode
  N7: Q2.G, D2.C
  N8: Q2.D, D1.A, L1.pin1
  N9: D1.C, BAT1.V+, L1.pin2
