# Fritzing sketch rasp-adafruit (saved by Fritzing 0.9.3b)
breadboards: 1

parts:
  Raspberry_Pi1 = Raspberry Pi 2
  R4 = Resistor [tolerance=±5% resistance=330 package=THT]
  Q2 = MOSFET-NCHANNEL [package=to220v]
  D1 = Diode [package=diode-1n4001]
  D2 = Diode [package=diode-1n4001]
  BAT1 = BC9VPC [package=bc9vpc]
  L1 = Solenoid
  LED4 = LED - 5mm [color="Green (565nm)" package="5 mm [THT]"]
  LED5 = smd LED [color="Red (633nm)" package="0805 [SMD]"]
  R5 = Resistor [tolerance=±5% resistance=330 package=THT]
  Part1 = Adafruit PN532 Breakout [part_number="Adafruit #364"]

nets:
  N1: Raspberry_Pi1.GPIO17, LED5.anode
  N2: Raspberry_Pi1.GPIO27, LED4.anode
  N3: Raspberry_Pi1.GPIO22, D2.A
  GND: Raspberry_Pi1.GND, R4.Pin_0, Q2.S, BAT1.V-, R5.Pin_0, Part1.GND, Part1.SEL0, Part1.SEL1
  N4: Raspberry_Pi1.GPIO15, Part1.NSS/SCL/RX
  N5: Raspberry_Pi1.GPIO14, Part1.MOSI/SDA/TX
  N6: Raspberry_Pi1.5V, Part1.+5.0V
  N7: R4.Pin_1, LED5.cathode
  N8: Q2.G, D2.C
  N9: Q2.D, D1.A, L1.pin1
  N10: D1.C, BAT1.V+, L1.pin2
  N11: LED4.cathode, R5.Pin_1

custom parts:
  Adafruit PN532 Breakout: The PN532 is the most popular NFC chip, and is what is embedded in pretty much every phone or device that does NFC. It can pretty much do it all, such as read and write to tags and cards, communicate with phones (say for payment processing), and 'act' like a NFC tag. If you want to do any sort of embedded NFC work, this is the chip you'll want to use! NFC (Near Field Communications) is a way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
