# Fritzing sketch rasp-elechouse (saved by Fritzing 0.9.3b)
breadboards: 1

parts:
  Raspberry_Pi1 = Raspberry Pi 2
  R4 = Resistor [tolerance=±5% resistance=330 package=THT]
  Q2 = MOSFET-NCHANNEL [package=to220v]
  D1 = Diode [package=diode-1n4001]
  D2 = Diode [package=diode-1n4001]
  BAT1 = BC9VPC [package=bc9vpc]
  L1 = Solenoid
  LED4 = LED - 5mm [color="Green (565nm)" package="5 mm [THT]"]
  LED5 = smd LED [color="Red (633nm)" package="0805 [SMD]"]
  R5 = Resistor [tolerance=±5% resistance=330 package=THT]

nets:
  N1: Raspberry_Pi1.GPIO17, LED5.anode
  N2: Raspberry_Pi1.GPIO27, LED4.anode
  N3: Raspberry_Pi1.GPIO22, D2.A
  N4: Raspberry_Pi1.GND, R4.Pin_0, Q2.S, BAT1.V-, R5.Pin_0
  N5: R4.Pin_1, LED5.cathode
  N6: Q2.G, D2.C
  N7: Q2.D, D1.A, L1.pin1
  N8: D1.C, BAT1.V+, L1.pin2
  N9: LED4.cathode, R5.Pin_1
